# Fritzing sketch kastelujarjestelma_projekti (saved by Fritzing 0.9.3b)
breadboards: 1

parts:
  Part1 = Arduino Uno (Rev3) - ICSP
  LCD1 = LCD screen
  R1 = Resistor [tolerance=±5% resistance=220 package=THT]
  LED1 = LED - 5mm [color="Red (633nm)" package="5 mm [THT]"]
  R2 = Resistor [tolerance=±5% resistance=220 package=THT]
  R3 = Trimmer Potentiometer [maximum_resistance=10kΩ package=THT]
  Part2 = FC-28 Soil Hygrometer Module
  Part3 = FC-28 Soil Hygrometer Module - Probe

nets:
  N1: Part1.A0, Part2.AO
  N2: Part1.ICSP_MOSI, Part1.D11_PWM/MOSI, LCD1.E
  N3: Part1.D10_PWM/SS, Part2.VCC
  N4: Part1.D12/MISO, LCD1.RS
  N5: Part1.D13/SCK, LED1.cathode
  N6: Part1.D2, LCD1.DB7
  N7: Part1.D3_PWM, LCD1.DB6
  N8: Part1.D4, LCD1.DB5
  N9: Part1.D5_PWM, LCD1.DB4
  5V: Part1.5V, LCD1.VDD, R1.Pin_0, R2.Pin_0, R3.leg2
  GND: Part1.GND, LCD1.VSS, LCD1.R/W, LCD1.LED-, R3.leg1, Part2.GND
  N10: LCD1.V0, R3.wiper
  N11: LCD1.LED+, R1.Pin_1
  N12: LED1.anode, R2.Pin_1
  N13: Part2.POS, Part3.POS
  N14: Part2.NEG, Part3.NEG

custom parts:
  FC-28 Soil Hygrometer Module: The FC-28 is a soil hygrometer module that uses the Texas Instruments LM393 comparator chip to provide an analog measurement of soil humidity. The digital output is high when soil moisture is over a certain threshold, as determined by adjusting the potentiometer.
  FC-28 Soil Hygrometer Module - Probe: The FC-28 is a soil hygrometer module that uses the Texas Instruments LM393 comparator chip to provide an analog measurement of soil humidity.
